# Fritzing sketch avr_prog_adaptor_vero (saved by Fritzing 0.7.11b)
stripboards: 1

parts:
  ZIF_SOCKET1 = Aries 28-6574-10 28W ZIF Socket [part_number=28-6574-10]
  J1 = shrouded pin header, 10 pins [form="♂ (shrouded male)"]
  R1 = Resistor [tolerance=±5% resistance=10k package=THT]
  Y1 = Resonator [frequency="8 MHz" package=THT]

nets:
  N1: ZIF_SOCKET1.Pin_1, J1.pin3, R1.Pin_0
  N2: ZIF_SOCKET1.Pin_7, J1.pin10, R1.Pin_1
  GND: ZIF_SOCKET1.Pin_8, ZIF_SOCKET1.Pin_22, J1.pin6, Y1.GND
  N3: ZIF_SOCKET1.Pin_9, Y1.0
  N4: ZIF_SOCKET1.Pin_10, Y1.pin_1
  MOSI: ZIF_SOCKET1.Pin_17, J1.pin1
  MISO: ZIF_SOCKET1.Pin_18, J1.pin5
  SCK: ZIF_SOCKET1.Pin_19, J1.pin4

notes:
  Babyduino, AVR ATMega Programming Adaptor, 1A
