# Fritzing sketch babyduino_nc_board (saved by Fritzing 0.7.11b)

parts:
  R2 = Resistor [tolerance=±5% resistance=220 package=THT]
  R1 = Resistor [tolerance=±5% resistance=10k package=THT]
  IC2 = FTDI [package=SIL]
  IC1 = ATMega8 [package=DIL]
  LED1 = LED - 5mm [color="Red (633nm)" package="5 mm [THT]"]
  IC3 = Babyduino [package=SIL]
  Y1 = Resonator [frequency="16 Mhz" package=THT]
  J1 = male pin header, 2 pins [form="♂ (male)"]
  C1 = Ceramic Capacitor [capacitance=100nF package="100 mil [THT, multilayer]"]

nets:
  D13: R2.Pin_0, IC1.SCK/PB5, IC3.D0
  N1: R2.Pin_1, LED1.anode
  VCC: R1.Pin_0, IC1.VCC, IC1.AVCC, IC1.AREF, IC3.VCC, C1.1
  N2: R1.Pin_1, IC1.RESET/PC6, J1.pin1
  GND: IC2.GND/Black, IC1.GND, LED1.cathode, IC3.GND, Y1.GND, J1.pin2, C1.0
  N3: IC2.TX, IC1.Rx/PD0, IC3.D5
  N4: IC2.RX, IC1.Tx/PD1, IC3.D6
  N5: IC1.INT0/PD2, IC3.D7
  N6: IC1.INT1/PD3, IC3.D8
  N7: IC1.XCK/T0/PD4, IC3.D9
  N8: IC1.XTAL1/TOSC1/PB6, Y1.0
  N9: IC1.XTAL2/TOSC2/PB7, Y1.pin_1
  N10: IC1.T1/PD5, IC3.D10
  N11: IC1.AIN0/PD6, IC3.D11
  N12: IC1.AIN1/PD7, IC3.D12
  N13: IC1.ICP1/PB0, IC3.D13
  D9: IC1.OC1A/PB1, IC3.D4
  D10: IC1.OC1B/SS/PB2, IC3.D3
  D11: IC1.MOSI/OC2/PB3, IC3.D2
  D12: IC1.MISO/PB4, IC3.D1
  A0: IC1.ADC0/PC0, IC3.A5
  A1: IC1.ADC1/PC1, IC3.A4
  A2: IC1.ADC2/PC2, IC3.A3
  A3: IC1.ADC3/PC3, IC3.A2
  A4: IC1.ADC4/SDA/PC4, IC3.A1
  A5: IC1.ADC5/SCL/PC5, IC3.A0

notes:
  Babyduino XC/NC
  http://thegaragelab.com
  FTDI
